# Fritzing sketch circuit (saved by Fritzing 0.9.2b)
breadboards: 1

parts:
  U1 = 7-SEGMENT-DISPLAY [package=7-segment-display]
  R1 = Resistor [tolerance=±5% resistance=220 package=THT]
  R2 = Resistor [tolerance=±5% resistance=220 package=THT]
  R3 = Resistor [tolerance=±5% resistance=220 package=THT]
  R4 = Resistor [tolerance=±5% resistance=220 package=THT]
  R5 = Resistor [tolerance=±5% resistance=220 package=THT]
  R6 = Resistor [tolerance=±5% resistance=220 package=THT]
  R7 = Resistor [tolerance=±5% resistance=220 package=THT]
  R8 = Resistor [tolerance=±5% resistance=220 package=THT]
  パーツ1 = Arduino Uno (Rev3)

nets:
  N1: U1.E, R4.Pin_1
  N2: U1.D, R8.Pin_1
  N3: U1.G1, R6.Pin_1
  N4: U1.C, パーツ1.GND
  N5: U1.DP, R5.Pin_0
  N6: U1.B, R7.Pin_0
  N7: U1.A, R2.Pin_0
  N8: U1.G2, R1.Pin_0
  N9: U1.G, R3.Pin_1
  N10: R1.Pin_1, パーツ1.D2
  N11: R2.Pin_1, パーツ1.D3_PWM
  N12: R3.Pin_0, パーツ1.D7
  N13: R4.Pin_0, パーツ1.D8
  N14: R5.Pin_1, パーツ1.D4
  N15: R6.Pin_0, パーツ1.D6_PWM
  N16: R7.Pin_1, パーツ1.D9_PWM
  N17: R8.Pin_0, パーツ1.D5_PWM

// code stored in the sketch: Untitled.ino

